// Logisim project variant-pcp6_1.circ as structural Verilog: 15 circuits, main circuit ◆单总线CPU(3级时序)
module \单总线CPU_3级时序  (
  output [21:0] \控制总线 ,
  output [31:0] pc,
  output [31:0] ir,
  output [31:0] imm32,
  output [31:0] ar,
  output [31:0] dr,
  output [31:0] x,
  output [31:0] z,
  output [31:0] bus,
  output [21:0] ctrl,
  output halt
);

  wire and_1_out, CLK, comparator_1_eq, equal, Mcal, Mex, Mif, Mint, mips_alu_1_equal, not_1_out, T1, T2, T3,
       T4;
  wire [4:0] registerfile_1_p4, registerfile_1_p5;
  wire [7:0] counter_2_p2;
  wire [11:0] Clks, \指令数 ;
  wire [31:0] controlled_buffer_1_out, controlled_buffer_2_out, mips_alu_1_result, ram_1_data,
       registerfile_1_p6, shifter_1_out;

  LED #(.active("true")) led_1 (.in(Mcal));
  LED #(.active("true")) led_2 (.in(Mif));
  // Probe on Clks
  Register #(.width(32), .trigger("rising"), .Select("low")) u_AR (
    .D(bus), .en(ctrl[13]), .Q({ar[31:10], ar[11:10], ar[11:10], ar[11:10], ar[11:10], ar[11:10]}), .clk(CLK));  // open: clr
  // Digital_Oscilloscope #(.nState(35), .frontlines("rising"), .showclock("true")) digital_oscilloscope_1: pin names not known; wires that end beside it: CLK, Mif, Mcal, Mex, T1, T2, T3, T4, ctrl[2]
  LED #(.active("true")) led_3 (.in(Mint));
  LED #(.active("true")) led_4 (.in(Mex));
  LED #(.active("true")) led_5 (.in(T1));
  // Mips_Probe mips_probe_1: pin names not known; wires that end beside it: ir
  // Probe on controlled_buffer_1_out
  Register #(.width(32), .trigger("rising"), .Select("low")) u_X (
    .D(bus), .en(ctrl[10]), .Q(x), .clk(CLK));  // open: clr
  LED #(.active("true")) led_6 (.in(T2));
  LED #(.active("true")) led_7 (.in(T3));
  // Probe on \指令数 
  LED #(.active("true")) led_8 (.in(T4));
  RAM #(.addrWidth(10), .dataWidth(32), .bus("separate"), .Select("high")) ram_1 (
    .addr({ar[11:10], ar[11:10], ar[11:10], ar[11:10], ar[11:10]}), .din(controlled_buffer_1_out),
    .data(ram_1_data), .str(ctrl[0]), .sel(1'b1), .clk(CLK), .ld(ctrl[1]));  // open: clr
  assign controlled_buffer_1_out = ctrl[15] ? dr : 32'bz;  // Controlled_Buffer controlled_buffer_1
  MIPS_ALU mips_alu_1 (
    .X(x), .Y(bus), .Equal(mips_alu_1_equal), .Result(mips_alu_1_result), .ADD(ctrl[4]), .ADD4(ctrl[3]),
    .SLT(ctrl[2]));  // open: SUB
  assign controlled_buffer_2_out = ctrl[11] ? bus : 32'bz;  // Controlled_Buffer controlled_buffer_2
  assign controlled_buffer_2_out = ctrl[12] ? ram_1_data : 32'bz;  // Controlled_Buffer controlled_buffer_3
  // Probe on bus
  assign bus = ctrl[21] ? bus : 32'bz;  // Controlled_Buffer controlled_buffer_4
  Register #(.width(32), .trigger("rising"), .Select("low")) u_PC (
    .D(bus), .en(ctrl[14]), .Q(bus), .clk(CLK), .clr(1'b0), .preset(1'b1));  // open: cs
  Register #(.width(32), .trigger("rising"), .Select("low")) u_DR (
    .D(controlled_buffer_2_out), .Q(dr), .clk(CLK));  // open: en, clr
  assign bus = ctrl[20] ? dr : 32'bz;  // Controlled_Buffer controlled_buffer_5
  Register #(.width(1), .trigger("rising"), .Select("low")) PSW (
    .D(mips_alu_1_equal), .en(ctrl[7]), .Q(equal), .clk(CLK));  // open: clr
  Register #(.width(32), .trigger("rising"), .Select("low")) u_Z (
    .D(mips_alu_1_result), .Q(bus), .clk(CLK));  // open: en, clr
  assign bus = ctrl[19] ? bus : 32'bz;  // Controlled_Buffer controlled_buffer_6
  Register #(.width(32), .trigger("rising"), .Select("low")) u_IR (
    .D(bus), .en(ctrl[8]), .Q(ir), .clk(CLK));  // open: clr
  assign bus = ctrl[17] ? imm32 : 32'bz;  // Controlled_Buffer controlled_buffer_7
  assign bus = ctrl[16] ? shifter_1_out : 32'bz;  // Controlled_Buffer controlled_buffer_8
  \硬布线控制器  \u_硬布线控制器_1  (
    .\状态节拍信号 ({T4, T3, T2, T1, Mex, Mcal, Mif}), .CLK(CLK), .IR(ir), .ControlBus(ctrl), .EQUAL(equal));
  // RegisterFile registerfile_1: pin names not known; wires that end beside it: bus, CLK, ctrl[9], registerfile_1_p4, registerfile_1_p5, registerfile_1_p6
  assign imm32 = {{16{ir[15]}}, ir[15:0]};  // Bit_Extender bit_extender_1
  assign bus = ctrl[18] ? registerfile_1_p6 : 32'bz;  // Controlled_Buffer controlled_buffer_9
  Multiplexer #(.select(1), .width(5), .disabled("Z"), .enable("false")) multiplexer_1 (
    .in0(ir[25:21]), .in1(ir[20:16]), .out(registerfile_1_p5), .sel(ctrl[6]));
  Multiplexer #(.select(1), .width(5), .disabled("Z"), .enable("false")) multiplexer_2 (
    .in0(ir[20:16]), .in1(ir[15:11]), .out(registerfile_1_p4), .sel(ctrl[5]));
  not not_1 (not_1_out, comparator_1_eq);
  Comparator #(.width(32), .mode("twosComplement")) comparator_1 (
    .a(ir), .b(32'h1000ffff), .eq(comparator_1_eq));  // open: gt, lt
  Clock #(.highDuration(1), .lowDuration(1)) clock_1 (.out(CLK));
  Shifter #(.width(32), .shift("ll")) shifter_1 (.in(imm32), .\dist (5'b00010), .out(shifter_1_out));
  Counter #(.width(12), .max('hfff), .ongoal("wrap"), .trigger("falling"), .behavior("new")) counter_1 (
    .count(not_1_out), .Q(Clks), .clk(CLK));  // open: load, D, carry, clr, preset, down
  and and_1 (and_1_out, not_1_out, Mif, T1);
  // Counter #(.width(8), .max('hff), .ongoal("wrap"), .trigger("rising"), .behavior("old")) counter_2: pin names not known; wires that end beside it: CLK, {counter_2_p2[7:2], halt, counter_2_p2[0]}
  Counter #(.width(12), .max('hfff), .ongoal("wrap"), .trigger("falling"), .behavior("old")) counter_3 (
    .count(and_1_out), .Q(\指令数 ), .clk(CLK));  // open: load, D, carry, clr, preset
  // Pins of 10 and 32 bits meet at {ar[31:10], ar[11:10], ar[11:10], ar[11:10], ar[11:10], ar[11:10]}
  // Pins of 1 and 7 bits meet at {counter_2_p2[7:2], halt}

  assign ar[9:0] = {ar[11:10], ar[11:10], ar[11:10], ar[11:10], ar[11:10]};
  assign pc = bus;
  assign z = bus;
  assign \控制总线  = ctrl;

  // Other names for the same wires on the sheet: DBG_AR[31:0] = {ar[31:10], ar[11:10], ar[11:10], ar[11:10], ar[11:10], ar[11:10]};
  //   DBG_CTRL[21:0] = ctrl; Write = ctrl[0]; READ = ctrl[1]; Slt = ctrl[2]; Add4 = ctrl[3]; Add = ctrl[4];
  //   RegDst = ctrl[5]; RegTgt = ctrl[6]; PSWin = ctrl[7]; IRin = ctrl[8]; Rin = ctrl[9]; Xin = ctrl[10];
  //   DRin = ctrl[11]; DREin = ctrl[12]; ARin = ctrl[13]; PCin = ctrl[14]; DREout = ctrl[15]; IR_A_out = ctrl[16];
  //   IR_I_out = ctrl[17]; Rout = ctrl[18]; Zout = ctrl[19]; DRout = ctrl[20]; PCout = ctrl[21]; DBG_DR[31:0] = dr;
  //   DBG_IMM32[31:0] = imm32; DBG_IR[31:0] = ir; rd[4:0] = ir[15:11]; rt[4:0] = ir[20:16]; rs[4:0] = ir[25:21];
  //   DBG_X[31:0] = x; DBG_BUS[31:0] = bus; DBG_PC[31:0] = bus; DBG_Z[31:0] = bus; 内部总线[31:0] = bus;
  //   状态节拍信号[6:0] = {T4, T3, T2, T1, Mex, Mcal, Mif}

  // Notes on the sheet:
  //   单总线结构 MIPS CPU
  //   MEM
  //   外部总线
  //   contents of ram_1 (hex, n*v repeats v):
  //   2010ffff 20110000 ae300200 22100001 22310004 ae300200 22100001 22310004 ae300200 22100001 22310004
  //   ae300200 22100001 22310004 ae300200 22100001 22310004 ae300200 22100001 22310004 ae300200 22100001
  //   22310004 ae300200 20100000 2011001c 8e130200 8e340200 0274402a 11000002 ae330200 ae140200 2231fffc
  //   12110001 1000fff7 22100004 2011001c 12110001 1000fff3 1000ffff
  //   内部总线
  //   三级时序
  //   Immediate32
  //   AddressOffset32
endmodule

// 硬布线
module \硬布线控制器  (
  input  CLK,
  input  [31:0] IR,
  input  EQUAL,
  output [6:0] \状态节拍信号 ,
  output [21:0] ControlBus
);

  wire ADDI, BEQ, LW, Mcal, Mex, Mif, Other;
  wire [3:0] register_1_q, rom_1_data;
  wire [12:1] OCInput;
  wire [21:0] ControlBus_old;

  Register #(.width(4), .trigger("rising"), .Select("low")) register_1 (
    .D(rom_1_data), .en(1'b1), .Q(register_1_q), .clk(CLK), .clr(1'b0), .cs(1'b0), .preset(1'b0));
  ROM #(.addrWidth(4), .dataWidth(4), .Select("low")) rom_1 (.addr(register_1_q), .data(rom_1_data), .sel(1'b0));
  ROM #(.addrWidth(4), .dataWidth(7), .Select("low")) rom_2 (
    .addr(register_1_q), .data({Mif, Mcal, Mex, OCInput[4:1]}), .sel(1'b0));
  \指令译码器  \u_指令译码器_1  (
    .IR(IR), .LW(LW), .SW(OCInput[9]), .BEQ(BEQ), .ADDI(ADDI), .SLT(OCInput[12]), .OtherInstr(Other));
  Pull_Resistor #(.pull(0)) pull_resistor_1 (.node(LW));
  Pull_Resistor #(.pull(0)) pull_resistor_2 (.node(OCInput[9]));
  Pull_Resistor #(.pull(0)) pull_resistor_3 (.node(BEQ));
  Pull_Resistor #(.pull(0)) pull_resistor_4 (.node(OCInput[12]));
  Pull_Resistor #(.pull(0)) pull_resistor_5 (.node(ADDI));
  \硬布线控制器组合逻辑单元  \u_硬布线控制器组合逻辑单元_1  (
    .SLT(OCInput[12]), .ADDI(ADDI), .LW(LW), .SW(OCInput[9]), .BEQ(BEQ), .Mif(Mif), .Mcal(Mcal), .Mex(Mex),
    .T1(OCInput[4]), .T2(OCInput[3]), .T3(OCInput[2]), .T4(OCInput[1]), .EQUAL(EQUAL),
    .Pcout(ControlBus_old[21]), .DRout(ControlBus_old[20]), .Zout(ControlBus_old[19]),
    .Rout(ControlBus_old[18]), .IRiout(ControlBus_old[17]), .IRaout(ControlBus_old[16]),
    .DREout(ControlBus_old[15]), .Pcin(ControlBus_old[14]), .ARin(ControlBus_old[13]),
    .DREin(ControlBus_old[12]), .DRin(ControlBus_old[11]), .Xin(ControlBus_old[10]), .Rin(ControlBus_old[9]),
    .IRin(ControlBus_old[8]), .PSWin(ControlBus_old[7]), .RegTgt(ControlBus_old[6]),
    .RegDst(ControlBus_old[5]), .Add(ControlBus_old[4]), .Add4(ControlBus_old[3]), .Slt_2(ControlBus_old[2]),
    .READ(ControlBus_old[1]), .WRITE(ControlBus_old[0]));
  ROM #(.addrWidth(13), .dataWidth(22), .Select("low")) rom_3 (
    .addr({OCInput[12], ADDI, LW, OCInput[9], BEQ, Mif, Mcal, Mex, OCInput[4:1], EQUAL}), .data(ControlBus),
    .sel(1'b0));

  // Other names for the same wires on the sheet: Write = ControlBus[0]; READ = ControlBus[1]; Slt_t = ControlBus[2];
  //   Add4 = ControlBus[3]; Add = ControlBus[4]; RegDst = ControlBus[5]; RegTgt = ControlBus[6];
  //   PSWin = ControlBus[7]; IRin = ControlBus[8]; Rin = ControlBus[9]; Xin = ControlBus[10]; DRin = ControlBus[11];
  //   DREin = ControlBus[12]; ARin = ControlBus[13]; PCin = ControlBus[14]; DREout = ControlBus[15];
  //   IR_A_out = ControlBus[16]; IR_I_out = ControlBus[17]; Rout = ControlBus[18]; Zout = ControlBus[19];
  //   DRout = ControlBus[20]; PCout = ControlBus[21]; OCInput (some bits) = {ADDI, LW, BEQ, Mif, Mcal, Mex, EQUAL};
  //   T4 = OCInput[1]; T3 = OCInput[2]; T2 = OCInput[3]; T1 = OCInput[4]; SW = OCInput[9]; SLT = OCInput[12];
  //   指令字[31:0] = IR

  // Notes on the sheet:
  //   不要改变此引脚区域内容，也不要改变封装形式
  //   指令译码信号
  //   状态寄存器
  //   状态寄存器应该下跳沿？
  //   现态
  //   FSM状态机
  //   次态
  //   状态机
  //   contents of rom_1 (hex, n*v repeats v):
  //   1 2 3 4 5 6 7 8 9 a b 0 0 0 0 0
  //   输出函数
  //   contents of rom_2 (hex, n*v repeats v):
  //   48 44 42 41 28 24 22 21 18 14 12 11 00 00 00 00
  //   输入输出引脚
  //   时序发生器TG
  //   指令译码器
  //   如发现控制信号有错可以直接查看具体哪位信号出错
  //   指令译码信号
  //   指令译码逻辑ID
  //   硬布线控制器组合逻辑单元
  //   contents of rom_3 (hex, n*v repeats v):
  //   000000 000000 000000 000000 000000 000000 000000 000000 000000 000000 000000 000000 000000 000000
  //   000000 000000 000000 000000 000000 000000 000000 000000 000000 000000 000000 000000 000000 000000
  //   000000 000000 000000 000000 000000 000000 000000 000000 000000 000000 000000 000000 000000 000000
  //   000000 000000 000000 000000 000000 000000 000000 000000 000000 000000 000000 000000 000000 000000
  //   000000 000000 000000 000000 000000 000000 000000 000000 000000 000000 000000 000000 080220 080220
  //   080220 080220 040050 040050 040050 040050 040050 040050 040050 040050 040400 040400 040400 040400
  //   040400 040400 040400 040400 040400 040400 040400 040400 040400 040400 040400 040400 000000 000000
  //   000000 000000 080220 080220 080220 080220 040050 040050 040050 040050 040050 040050 040050 040050
  //   040400 040400 040400 040400 040400 040400 040400 040400 040400 040400 040400 040400 040400 040400
  //   040400 040400 000000 000000 100100 100100 085002 085002 085002 085002 000008 000008 000008 000008
  //   000008 000008 000008 000008 202400 202400 202400 202400 202400 202400 202400 202400 202400 202400
  //   202400 202400 202400 202400 202400 202400 000000 000000 100100 100100 085002 085002 085002 085002
  //   000008 000008 000008 000008 000008 000008 000008 000008 202400 202400 202400 202400 202400 202400
  //   202400 202400 202400 202400 202400 202400 202400 202400 202400 202400 000000 000000 100100 100100
  //   085002 085002 085002 085002 000008 000008 000008 000008 000008 000008 000008 000008 202400 202400
  //   202400 202400 202400 202400 202400 202400 202400 202400 202400 202400 202400 202400 202400 202400
  //   000000 000000 100100 100100 085002 085002 085002 085002 000008 000008 000008 000008 000008 000008
  //   000008 000008 202400 202400 202400 202400 202400 202400 202400 202400 202400 202400 202400 202400
  //   202400 202400 202400 202400 000000 000000 000000 000000 000000 000000 000000 000000 000000 000000
  //   000000 000000 000000 000000 000000 000000 000000 000000 000000 000000 000000 000000 000000 000000
  //   000000 000000 000000 000000 000000 000000 000000 000000 000000 000000 000000 000000 000000 000000
  //   000000 000000 000000 000000 000000 000000 000000 000000 000000 000000 000000 000000 000000 000000
  //   000000 000000 000000 000000 000000 000000 000000 000000 000000 000000 000000 000000 000000 000000
  //   000000 000000 000000 084000 000000 084000 010010 010010 010010 010010 010010 010010 010010 010010
  //   200400 200400 200400 200400 200400 200400 200400 200400 200400 200400 200400 200400 200400 200400
  //   200400 200400 000000 000000 000000 000000 000000 084000 000000 084000 010010 010010 010010 010010
  //   010010 010010 010010 010010 200400 200400 200400 200400 200400 200400 200400 200400 200400 200400
  //   200400 200400 200400 200400 200400 200400 000000 000000 100100 100100 085002 085002 085002 085002
  //   000008 000008 000008 000008 000008 000008 000008 000008 202400 202400 202400 202400 202400 202400
  //   202400 202400 202400 202400 202400 202400 202400 202400 202400 202400 000000 000000 100100 100100
  //   085002 085002 085002 085002 000008 000008 000008 000008 000008 000008 000008 000008 202400 202400
  //   202400 202400 202400 202400 202400 202400 202400 202400 202400 202400 202400 202400 202400 202400
  //   000000 000000 100100 100100 085002 085002 085002 085002 000008 000008 000008 000008 000008 000008
  //   000008 000008 202400 202400 202400 202400 202400 202400 202400 202400 202400 202400 202400 202400
  //   202400 202400 202400 202400 000000 000000 100100 100100 085002 085002 085002 085002 000008 000008
  //   000008 000008 000008 000008 000008 000008 202400 202400 202400 202400 202400 202400 202400 202400
  //   202400 202400 202400 202400 202400 202400 202400 202400 000000 000000 000000 000000 000000 000000
  //   000000 000000 000000 000000 000000 000000 000000 000000 000000 000000 000000 000000 000000 000000
  //   000000 000000 000000 000000 000000 000000 000000 000000 000000 000000 000000 000000 000000 000000
  //   000000 000000 000000 000000 000000 000000 000000 000000 000000 000000 000000 000000 000000 000000
  //   008001 008001 008001 008001 008001 008001 008001 008001 008001 008001 008001 008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
endmodule

// Decoder
module \指令译码器  (
  input  [31:0] IR,
  output LW,
  output SW,
  output BEQ,
  output ADDI,
  output SLT,
  output OtherInstr
);

  Comparator #(.width(6), .mode("twosComplement")) comparator_1 ();  // open: a, b, gt, eq, lt
  nor nor_1 (OtherInstr, BEQ, SW, LW, ADDI, SLT);

  // Other names for the same wires on the sheet: FUNCT[5:0] = IR[5:0]; OP[5:0] = IR[31:26]

  // Notes on the sheet:
  //   常用常量
  //   请勿增删改引脚，否则可能引起子电路外观变化，无法自动测试
  //   将指令字IR转换成指令译码信息，每一个输出代表一条不同的指令
endmodule

module \时序发生器状态机_定长指令周期  (
  input  S3,
  input  S2,
  input  S1,
  input  S0,
  output N3,
  output N2,
  output N1,
  output N0
);

  ROM #(.addrWidth(4), .dataWidth(4), .Select("low")) rom_1 (
    .addr({S3, S2, S1, S0}), .data({N3, N2, N1, N0}), .sel(1'b0));

  // Other names for the same wires on the sheet: fsm_S0 = S0; fsm_S1 = S1; fsm_S2 = S2; fsm_S3 = S3; fsm_N0 = N0;
  //   fsm_N1 = N1; fsm_N2 = N2; fsm_N3 = N3

  // Notes on the sheet:
  //   contents of rom_1 (hex, n*v repeats v):
  //   1 2 3 4 5 6 7 8 9 a b 0 0 0 0 0
endmodule

module \时序发生器输出函数_定长指令周期  (
  input  S3,
  input  S2,
  input  S1,
  input  S0,
  output Mif,
  output Mcal,
  output Mex,
  output T1,
  output T2,
  output T3,
  output T4
);

  wire [1:0] rom_1_data;

  ROM #(.addrWidth(4), .dataWidth(7), .Select("low")) rom_1 (
    .addr({S3, S2, S1, S0}), .data({Mcal, T1, T2, T3, T4, rom_1_data}), .sel(1'b0));

  assign Mex = Mcal;

  // Other names for the same wires on the sheet: tg_S0 = S0; tg_S1 = S1; tg_S2 = S2; tg_S3 = S3; tg_T4 = T4;
  //   tg_T3 = T3; tg_T2 = T2; tg_T1 = T1; tg_Mcal = Mcal; tg_Mex = Mcal; tg_Mif = Mif

  // Notes on the sheet:
  //   contents of rom_1 (hex, n*v repeats v):
  //   48 44 42 41 28 24 22 21 18 14 12 11 00 00 00 00
endmodule

// 状态机
module \时序发生器状态机_变长指令周期  (
  input  LW,
  input  SW,
  input  BEQ,
  input  SLT,
  input  ADDI,
  input  S3,
  input  S2,
  input  S1,
  input  S0,
  output N3,
  output N2,
  output N1,
  output N0
);
endmodule

module \时序发生器输出函数_变长指令周期  (
  input  S3,
  input  S2,
  input  S1,
  input  S0,
  output Mif,
  output Mcal,
  output Mex,
  output T1,
  output T2,
  output T3,
  output T4
);
endmodule

module \硬布线控制器组合逻辑单元  (
  input  SLT,
  input  ADDI,
  input  LW,
  input  SW,
  input  BEQ,
  input  Mif,
  input  Mcal,
  input  Mex,
  input  T1,
  input  T2,
  input  T3,
  input  T4,
  input  EQUAL,
  output Pcout,
  output DRout,
  output Zout,
  output Rout,
  output IRiout,
  output IRaout,
  output DREout,
  output Pcin,
  output ARin,
  output DREin,
  output DRin,
  output Xin,
  output Rin,
  output IRin,
  output PSWin,
  output RegTgt,
  output RegDst,
  output Add,
  output Add4,
  output Slt_2,
  output READ,
  output WRITE
);

  wire ctl_eq_beq, ctl_phase_mem, ctl_safe_ADDI, ctl_safe_BEQ, ctl_safe_EQUAL, ctl_safe_LW, ctl_safe_SLT,
       ctl_safe_SW;
  wire [8:0] rom_1_data;
  wire [12:0] buffer_13_out;

  and and_1 (ctl_safe_SLT, SLT, Mcal);
  and and_2 (ctl_safe_ADDI, ADDI, Mcal);
  and and_3 (ctl_safe_LW, LW, ctl_phase_mem);
  and and_4 (ctl_safe_SW, SW, ctl_phase_mem);
  and and_5 (ctl_safe_BEQ, BEQ, Mcal);
  or or_1 (ctl_phase_mem, Mcal, Mex);
  and and_6 (ctl_eq_beq, EQUAL, ctl_safe_BEQ);
  buf buffer_1 (buffer_13_out[12], ctl_safe_SLT);
  buf buffer_2 (buffer_13_out[11], ctl_safe_ADDI);
  buf buffer_3 (buffer_13_out[10], ctl_safe_LW);
  buf buffer_4 (buffer_13_out[9], ctl_safe_SW);
  buf buffer_5 (buffer_13_out[8], ctl_safe_BEQ);
  buf buffer_6 (buffer_13_out[7], Mif);
  buf buffer_7 (buffer_13_out[6], Mcal);
  buf buffer_8 (buffer_13_out[5], Mex);
  buf buffer_9 (buffer_13_out[4], T1);
  buf buffer_10 (buffer_13_out[3], T2);
  buf buffer_11 (buffer_13_out[2], T3);
  buf buffer_12 (buffer_13_out[1], T4);
  buf buffer_13 (buffer_13_out[0], ctl_safe_EQUAL);
  and and_7 (ctl_safe_EQUAL, ctl_eq_beq, T3);
  ROM #(.addrWidth(13), .dataWidth(22), .Select("low")) rom_1 (
    .data({ARin, Xin, DRin, IRin, Rin, RegTgt, PSWin, Add, RegDst, Slt_2, Add4, WRITE, READ, rom_1_data}),
    .sel(1'b0));  // open: addr

  // Other names for the same wires on the sheet: ctl_READ = READ; ctl_WRITE = WRITE; ctl_Add4 = Add4; ctl_Slt = Slt_2;
  //   ctl_RegDst = RegDst; ctl_Add = Add; ctl_PSWin = PSWin; ctl_RegTgt = RegTgt; ctl_Rin = Rin; ctl_IRin = IRin;
  //   ctl_DRin = DRin; ctl_Xin = Xin; ctl_ARin = ARin; ctl_DREin = DREin; ctl_DREout = DREout; ctl_DRout = DRout;
  //   ctl_IRaout = IRaout; ctl_IRiout = IRiout; ctl_Pcin = Pcin; ctl_Pcout = Pcout; ctl_raw_ADDI = ADDI;
  //   ctl_raw_BEQ = BEQ; ctl_raw_EQUAL = EQUAL; ctl_raw_LW = LW; ctl_raw_Mcal = Mcal; ctl_raw_Mex = Mex;
  //   ctl_raw_Mif = Mif; ctl_raw_SLT = SLT; ctl_raw_SW = SW; ctl_raw_T1 = T1; ctl_raw_T2 = T2; ctl_raw_T3 = T3;
  //   ctl_raw_T4 = T4; ctl_Rout = Rout; ctl_Zout = Zout

  // Notes on the sheet:
  //   contents of rom_1 (hex, n*v repeats v):
  //   000000 000000 000000 000000 000000 000000 000000 000000 000000 000000 000000 000000 000000 000000
  //   000000 000000 000000 000000 000000 000000 000000 000000 000000 000000 000000 000000 000000 000000
  //   000000 000000 000000 000000 000000 000000 000000 000000 000000 000000 000000 000000 000000 000000
  //   000000 000000 000000 000000 000000 000000 000000 000000 000000 000000 000000 000000 000000 000000
  //   000000 000000 000000 000000 000000 000000 000000 000000 000000 000000 000000 000000 040110 040110
  //   040110 040110 0800a0 0800a0 0800a0 0800a0 0800a0 0800a0 0800a0 0800a0 080800 080800 080800 080800
  //   080800 080800 080800 080800 080800 080800 080800 080800 080800 080800 080800 080800 000000 000000
  //   000000 000000 040110 040110 040110 040110 0800a0 0800a0 0800a0 0800a0 0800a0 0800a0 0800a0 0800a0
  //   080800 080800 080800 080800 080800 080800 080800 080800 080800 080800 080800 080800 080800 080800
  //   080800 080800 000000 000000 200200 200200 04a001 04a001 04a001 04a001 000004 000004 000004 000004
  //   000004 000004 000004 000004 101800 101800 101800 101800 101800 101800 101800 101800 101800 101800
  //   101800 101800 101800 101800 101800 101800 000000 000000 200200 200200 04a001 04a001 04a001 04a001
  //   000004 000004 000004 000004 000004 000004 000004 000004 101800 101800 101800 101800 101800 101800
  //   101800 101800 101800 101800 101800 101800 101800 101800 101800 101800 000000 000000 200200 200200
  //   04a001 04a001 04a001 04a001 000004 000004 000004 000004 000004 000004 000004 000004 101800 101800
  //   101800 101800 101800 101800 101800 101800 101800 101800 101800 101800 101800 101800 101800 101800
  //   000000 000000 200200 200200 04a001 04a001 04a001 04a001 000004 000004 000004 000004 000004 000004
  //   000004 000004 101800 101800 101800 101800 101800 101800 101800 101800 101800 101800 101800 101800
  //   101800 101800 101800 101800 000000 000000 000000 000000 000000 000000 000000 000000 000000 000000
  //   000000 000000 000000 000000 000000 000000 000000 000000 000000 000000 000000 000000 000000 000000
  //   000000 000000 000000 000000 000000 000000 000000 000000 000000 000000 000000 000000 000000 000000
  //   000000 000000 000000 000000 000000 000000 000000 000000 000000 000000 000000 000000 000000 000000
  //   000000 000000 000000 000000 000000 000000 000000 000000 000000 000000 000000 000000 000000 000000
  //   000000 000000 000000 048000 000000 048000 020020 020020 020020 020020 020020 020020 020020 020020
  //   100800 100800 100800 100800 100800 100800 100800 100800 100800 100800 100800 100800 100800 100800
  //   100800 100800 000000 000000 000000 000000 000000 048000 000000 048000 020020 020020 020020 020020
  //   020020 020020 020020 020020 100800 100800 100800 100800 100800 100800 100800 100800 100800 100800
  //   100800 100800 100800 100800 100800 100800 000000 000000 200200 200200 04a001 04a001 04a001 04a001
  //   000004 000004 000004 000004 000004 000004 000004 000004 101800 101800 101800 101800 101800 101800
  //   101800 101800 101800 101800 101800 101800 101800 101800 101800 101800 000000 000000 200200 200200
  //   04a001 04a001 04a001 04a001 000004 000004 000004 000004 000004 000004 000004 000004 101800 101800
  //   101800 101800 101800 101800 101800 101800 101800 101800 101800 101800 101800 101800 101800 101800
  //   000000 000000 200200 200200 04a001 04a001 04a001 04a001 000004 000004 000004 000004 000004 000004
  //   000004 000004 101800 101800 101800 101800 101800 101800 101800 101800 101800 101800 101800 101800
  //   101800 101800 101800 101800 000000 000000 200200 200200 04a001 04a001 04a001 04a001 000004 000004
  //   000004 000004 000004 000004 000004 000004 101800 101800 101800 101800 101800 101800 101800 101800
  //   101800 101800 101800 101800 101800 101800 101800 101800 000000 000000 000000 000000 000000 000000
  //   000000 000000 000000 000000 000000 000000 000000 000000 000000 000000 000000 000000 000000 000000
  //   000000 000000 000000 000000 000000 000000 000000 000000 000000 000000 000000 000000 000000 000000
  //   000000 000000 000000 000000 000000 000000 000000 000000 000000 000000 000000 000000 000000 000000
  //   004002 004002 004002 004002 004002 004002 004002 004002 004002 004002 004002 004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
endmodule

module \单总线CPU_中断_3级时序  (
  input  [1:0] EduInt,
  output [21:0] \EDU控制总线 ,
  output [4:0] \EDU中断信号 
);

  wire _1_out, _2_out, and_1_out, CLK, comparator_1_eq, equal, Mcal, Mex, Mif, Mint, mips_alu_1_equal,
       not_1_out, T1, T2, T3, T4, \中断控制器_1_ir1w , \中断控制器_1_ir2w , \中断请求 ;
  wire [4:0] registerfile_1_p5, registerfile_1_p6;
  wire [11:0] Clks, \指令数 ;
  wire [31:0] AR_q, bit_extender_1_out, controlled_buffer_1_out, controlled_buffer_3_out, DR_q, IR,
       mips_alu_1_result, PC_q, ram_1_data, registerfile_1_p7, shifter_1_out, X_q, Z_q, \内部总线 ;

  LED #(.active("true")) led_1 (.in(Mif));
  LED #(.active("true")) led_2 (.in(Mex));
  LED #(.active("true")) led_3 (.in(Mcal));
  LED #(.active("true")) led_4 (.in(Mint));
  // Probe on Clks
  Register #(.width(32), .trigger("rising"), .Select("low")) AR (
    .D(\内部总线 ), .en(\EDU控制总线 [13]), .Q(AR_q), .clk(CLK));  // open: clr
  // Probe on controlled_buffer_3_out
  // Digital_Oscilloscope #(.nState(35), .frontlines("rising"), .showclock("true")) digital_oscilloscope_1: pin names not known; wires that end beside it: CLK, Mif, Mcal, Mex, Mint, T1, T2, T3, T4
  LED #(.active("true")) led_5 (.in(T1));
  LED #(.active("true")) led_6 (.in(T2));
  // Mips_Probe mips_probe_1: pin names not known; wires that end beside it: IR
  Register #(.width(32), .trigger("rising"), .Select("low")) X (
    .D(\内部总线 ), .en(\EDU控制总线 [10]), .Q(X_q), .clk(CLK));  // open: clr
  LED #(.active("true")) led_7 (.in(T4));
  LED #(.active("true")) led_8 (.in(T3));
  // Probe on \指令数 
  RAM #(.addrWidth(10), .dataWidth(32), .bus("separate"), .Select("high")) ram_1 (
    .addr(AR_q[11:2]), .din(controlled_buffer_3_out), .data(ram_1_data), .str(\EDU控制总线 [0]), .sel(1'b1),
    .clk(CLK), .ld(\EDU控制总线 [1]));  // open: clr
  MIPS_ALU mips_alu_1 (
    .X(X_q), .Y(\内部总线 ), .Equal(mips_alu_1_equal), .Result(mips_alu_1_result), .ADD(\EDU控制总线 [4]),
    .ADD4(\EDU控制总线 [3]), .SLT(\EDU控制总线 [2]));  // open: SUB
  assign controlled_buffer_1_out = \EDU控制总线 [11] ? \内部总线  : 32'bz;  // Controlled_Buffer controlled_buffer_1
  assign controlled_buffer_1_out = \EDU控制总线 [12] ? ram_1_data : 32'bz;  // Controlled_Buffer controlled_buffer_2
  assign controlled_buffer_3_out = \EDU控制总线 [15] ? DR_q : 32'bz;  // Controlled_Buffer controlled_buffer_3
  // Probe on \内部总线 
  Register #(.width(32), .trigger("rising"), .Select("low")) PC (
    .D(\内部总线 ), .en(\EDU控制总线 [14]), .Q(PC_q), .clk(CLK));  // open: clr
  Register #(.width(32), .trigger("rising"), .Select("low")) DR (
    .D(controlled_buffer_1_out), .Q(DR_q), .clk(CLK));  // open: en, clr
  Register #(.width(1), .trigger("rising"), .Select("low")) PSW (
    .D(mips_alu_1_equal), .en(\EDU控制总线 [7]), .Q(equal), .clk(CLK));  // open: clr
  Register #(.width(32), .trigger("rising"), .Select("low")) Z (
    .D(mips_alu_1_result), .Q(Z_q), .clk(CLK));  // open: en, clr
  assign \内部总线  = \EDU控制总线 [21] ? PC_q : 32'bz;  // Controlled_Buffer controlled_buffer_4
  // Probe on \内部总线 
  assign \内部总线  = \EDU控制总线 [20] ? DR_q : 32'bz;  // Controlled_Buffer controlled_buffer_5
  assign \内部总线  = \EDU控制总线 [19] ? Z_q : 32'bz;  // Controlled_Buffer controlled_buffer_6
  assign \内部总线  = \EDU控制总线 [17] ? bit_extender_1_out : 32'bz;  // Controlled_Buffer controlled_buffer_7
  assign \内部总线  = \EDU控制总线 [16] ? shifter_1_out : 32'bz;  // Controlled_Buffer controlled_buffer_8
  Register #(.width(32), .trigger("rising"), .Select("low")) u_IR (
    .D(\内部总线 ), .en(\EDU控制总线 [8]), .Q(IR), .clk(CLK));  // open: clr
  \硬布线控制器_中断  \u_硬布线控制器_中断_1  (
    .CLK(CLK), .IR(IR), .EQUAL(equal), .M_T({Mif, Mcal, Mex, Mint, T1, T2, T3, T4}), .ControlBus(\EDU控制总线 ),
    .IntSignals(\EDU中断信号 ), .IntR(\中断请求 ));
  // RegisterFile registerfile_1: pin names not known; wires that end beside it: \内部总线 , CLK, \EDU控制总线 [15], \EDU控制总线 [9], registerfile_1_p5, registerfile_1_p6, registerfile_1_p7
  assign bit_extender_1_out = {{16{IR[15]}}, IR[15:0]};  // Bit_Extender bit_extender_1
  assign \内部总线  = \EDU控制总线 [18] ? registerfile_1_p7 : 32'bz;  // Controlled_Buffer controlled_buffer_9
  Multiplexer #(.select(1), .width(5), .disabled("Z"), .enable("false")) multiplexer_1 (
    .in0(IR[25:21]), .in1(IR[20:16]), .out(registerfile_1_p6), .sel(\EDU控制总线 [6]));
  Multiplexer #(.select(1), .width(5), .disabled("Z"), .enable("false")) multiplexer_2 (
    .in0(IR[20:16]), .in1(IR[15:11]), .out(registerfile_1_p5), .sel(\EDU控制总线 [5]));
  Shifter #(.width(32), .shift("ll")) shifter_1 (.in(bit_extender_1_out), .\dist (5'b00010), .out(shifter_1_out));
  D_Flip_Flop #(.trigger("rising"), .Pre_Clr_Positions("LEGACY"), .NegatePresetClear("false"), .enable("true"), .NewFFLayout("false")) d_ff_1 (
    .preset(\EDU中断信号 [0]), .reset(\EDU中断信号 [1]));  // open: clk, D, Q, Qn, en
  Button _1 (.out(_1_out));
  Button _2 (.out(_2_out));
  Comparator #(.width(32), .mode("twosComplement")) comparator_1 (
    .a(IR), .b(32'h1000ffff), .eq(comparator_1_eq));  // open: gt, lt
  Register #(.width(32), .trigger("rising"), .Select("low")) EPC (.clk(CLK));  // open: D, en, Q, clr
  LED #(.active("true")) _1_2 (.in(\中断控制器_1_ir1w ));
  LED #(.active("true")) _2_2 (.in(\中断控制器_1_ir2w ));
  \中断控制器  \u_中断控制器_1  (
    .CLK(CLK), .Key1(_1_out), .Key2(_2_out), .Clr(\EDU中断信号 [1]), .IR1W(\中断控制器_1_ir1w ),
    .IR2W(\中断控制器_1_ir2w ), .EDU_TEST(EduInt));  // open: IR3W, IntNo, IntR, Key3
  Counter #(.width(12), .max('hfff), .ongoal("wrap"), .trigger("falling"), .behavior("new")) counter_1 (
    .count(not_1_out), .Q(Clks), .clk(CLK));  // open: load, D, carry, clr, preset, down
  not not_1 (not_1_out, comparator_1_eq);
  Clock #(.highDuration(1), .lowDuration(1)) clock_1 (.out(CLK));
  Counter #(.width(12), .max('hfff), .ongoal("wrap"), .trigger("falling"), .behavior("old")) counter_2 (
    .count(and_1_out), .Q(\指令数 ), .clk(CLK));  // open: load, D, carry, clr, preset
  and and_1 (and_1_out, not_1_out, Mif, T1);

  // Other names for the same wires on the sheet: rd[4:0] = IR[15:11]; rt[4:0] = IR[20:16]; rs[4:0] = IR[25:21];
  //   中断控制信号[4:0] = \EDU中断信号 ; 关中断 = \EDU中断信号 [0]; 开中断 = \EDU中断信号 [1]; Addrout = \EDU中断信号 [2]; EPCin = \EDU中断信号 [3];
  //   EPCout = \EDU中断信号 [4]; Write = \EDU控制总线 [0]; 控制总线[21:0] = \EDU控制总线 ; READ = \EDU控制总线 [1]; Slt = \EDU控制总线 [2];
  //   Add4 = \EDU控制总线 [3]; Add = \EDU控制总线 [4]; RegDst = \EDU控制总线 [5]; RegTgt = \EDU控制总线 [6]; PSWin = \EDU控制总线 [7];
  //   IRin = \EDU控制总线 [8]; Rin = \EDU控制总线 [9]; Xin = \EDU控制总线 [10]; DRin = \EDU控制总线 [11]; DREin = \EDU控制总线 [12];
  //   ARin = \EDU控制总线 [13]; PCin = \EDU控制总线 [14]; DREout = \EDU控制总线 [15]; IR_A_out = \EDU控制总线 [16];
  //   IR_I_out = \EDU控制总线 [17]; Rout = \EDU控制总线 [18]; Zout = \EDU控制总线 [19]; DRout = \EDU控制总线 [20];
  //   PCout = \EDU控制总线 [21]; 状态节拍信号[7:0] = {Mif, Mcal, Mex, Mint, T1, T2, T3, T4}

  // Notes on the sheet:
  //   单总线结构 MIPS CPU+中断
  //   MEM
  //   contents of ram_1 (hex, n*v repeats v):
  //   2010ffff 20110000 ae300200 22100001 22310004 ae300200 22100001 22310004 ae300200 22100001 22310004
  //   ae300200 22100001 22310004 ae300200 22100001 22310004 ae300200 22100001 22310004 ae300200 22100001
  //   22310004 ae300200 20100000 2011001c 8e130200 8e340200 0274402a 11000002 ae330200 ae140200 2231fffc
  //   12110001 1000fff7 22100004 2011001c 12110001 1000fff3 1000ffff
  //   外部总线
  //   内部总线
  //   三级时序+中断
  //   Immediate32
  //   AddressOffset32
  //   中断使能寄存器
  //   EPC用于保存断点
  //   执行ERET时开中断，同时清除中断源
  //   中断逻辑
endmodule

// 控制器
module \硬布线控制器_中断  (
  input  CLK,
  input  [31:0] IR,
  input  EQUAL,
  input  IntR,
  output [7:0] M_T,
  output [21:0] ControlBus,
  output [4:0] IntSignals
);

  wire ADDI, BEQ, ERET, IntSignalsController_pcin, IntSignalsController_pcout, LW, PCin1, PCout1;
  wire [3:0] undriven;
  wire [12:9] OCInput;

  // 时序发生器状态机_中断 时序发生器状态机_中断_1: pin names not known; wires that end beside it: ADDI, OCInput[12]
  Register #(.width(4), .trigger("rising"), .Select("low")) register_1 ();  // open: D, en, Q, clk, clr
  \时序发生器输出函数_中断  \u_时序发生器输出函数_中断_1  (
    .S3(undriven[3]), .S2(undriven[2]), .S1(undriven[1]), .S0(undriven[0]), .Mif(M_T[7]), .Mcal(M_T[6]),
    .Mex(M_T[5]), .Mint(M_T[4]), .T1(M_T[3]), .T2(M_T[2]), .T3(M_T[1]), .T4(M_T[0]));
  \中断信号控制器  IntSignalsController (
    .ERET(ERET), .Mex(M_T[5]), .Mint(M_T[4]), .T1(M_T[3]), .T2(M_T[2]), .Pcout(IntSignalsController_pcout),
    .PCin(IntSignalsController_pcin), .EPCout(IntSignals[4]), .EPCin(IntSignals[3]), .Addrout(IntSignals[2]),
    .STI(IntSignals[1]), .CLI(IntSignals[0]));
  \指令译码器  \u_指令译码器_1  (.IR(IR), .LW(LW), .SW(OCInput[9]), .BEQ(BEQ), .ADDI(ADDI), .SLT(OCInput[12]), .OtherInstr(ERET));
  or or_1 (ControlBus[21], PCout1, IntSignalsController_pcout);
  or or_2 (ControlBus[14], IntSignalsController_pcin, PCin1);
  \硬布线控制器组合逻辑单元  \u_硬布线控制器组合逻辑单元_1  (
    .SLT(OCInput[12]), .ADDI(ADDI), .LW(LW), .SW(OCInput[9]), .BEQ(BEQ), .Mif(M_T[7]), .Mcal(M_T[6]),
    .Mex(M_T[5]), .T1(M_T[3]), .T2(M_T[2]), .T3(M_T[1]), .T4(M_T[0]), .EQUAL(EQUAL), .Pcout(PCout1),
    .DRout(ControlBus[20]), .Zout(ControlBus[19]), .Rout(ControlBus[18]), .IRiout(ControlBus[17]),
    .IRaout(ControlBus[16]), .DREout(ControlBus[15]), .Pcin(PCin1), .ARin(ControlBus[13]),
    .DREin(ControlBus[12]), .DRin(ControlBus[11]), .Xin(ControlBus[10]), .Rin(ControlBus[9]),
    .IRin(ControlBus[8]), .PSWin(ControlBus[7]), .RegTgt(ControlBus[6]), .RegDst(ControlBus[5]),
    .Add(ControlBus[4]), .Add4(ControlBus[3]), .Slt_2(ControlBus[2]), .READ(ControlBus[1]),
    .WRITE(ControlBus[0]));

  // Other names for the same wires on the sheet: PCin = ControlBus[14]; PCout = ControlBus[21]; Mint = M_T[4];
  //   OCInput (some bits) = {ADDI, LW, BEQ, M_T[7:5], M_T[3:0], EQUAL}; T4 = M_T[0]; T3 = M_T[1]; T2 = M_T[2];
  //   T1 = M_T[3]; Mex = M_T[5]; Mcal = M_T[6]; Mif = M_T[7]; SW = OCInput[9]; SLT = OCInput[12]; 指令字[31:0] = IR

  // Notes on the sheet:
  //   现态
  //   次态
  //   状态机
  //   中断控制相关信号生成逻辑
  //   不要改变此引脚区域内容，也不要改变封装形式
  //   指令译码信号
  //   状态寄存器
  //   状态寄存器应该下跳沿？
  //   状态寄存器应该下跳沿？
  //   FSM状态机
  //   输入输出引脚
  //   时序产生器TG
  //   指令译码器
  //   注意：IntSignals中的信号和上面的硬布线控制器组合逻辑单元无关，相关信号要合并处理
  //   指令译码信号
  //   指令译码逻辑ID
  //   操作控制器OC
endmodule

// 状态机
module \时序发生器状态机_中断  (
  input  ERET,
  input  LW,
  input  SW,
  input  BEQ,
  input  SLT,
  input  ADDI,
  input  IntR,
  input  S3,
  input  S2,
  input  S1,
  input  S0,
  output N3,
  output N2,
  output N1,
  output N0
);
endmodule

module \时序发生器输出函数_中断  (
  input  S3,
  input  S2,
  input  S1,
  input  S0,
  output Mif,
  output Mcal,
  output Mex,
  output Mint,
  output T1,
  output T2,
  output T3,
  output T4
);
endmodule

module \中断信号控制器  (
  input  ERET,
  input  Mex,
  input  Mint,
  input  T1,
  input  T2,
  output Pcout,
  output PCin,
  output EPCout,
  output EPCin,
  output Addrout,
  output STI,
  output CLI
);


  // Notes on the sheet:
  //   直接使用逻辑表达式生成，手写逻辑表达式
endmodule

// ALU
module MIPS_ALU (
  input  ADD,
  input  ADD4,
  input  [31:0] X,
  input  [31:0] Y,
  input  SUB,
  input  SLT,
  output Equal,
  output [31:0] Result
);

  wire [0:0] comparator_1_lt;
  wire [1:0] priority_encoder_1_out;
  wire [31:0] adder_1_out, adder_2_out, subtractor_1_out;

  Pull_Resistor #(.pull(0)) pull_resistor_1 (.node(Y));
  Adder #(.width(32)) adder_1 (.a(X), .b(Y), .out(adder_1_out));  // open: cin, cout
  Adder #(.width(32)) adder_2 (.a(X), .b(32'h4), .out(adder_2_out));  // open: cin, cout
  Subtractor #(.width(32)) subtractor_1 (.a(X), .b(Y), .out(subtractor_1_out));  // open: bin, bout
  Comparator #(.width(32), .mode("twosComplement")) comparator_1 (
    .a(X), .b(Y), .eq(Equal), .lt(comparator_1_lt[0]));  // open: gt
  Priority_Encoder #(.select(2), .disabled("Z")) priority_encoder_1 (
    .in0(ADD), .in1(ADD4), .in2(SUB), .in3(SLT), .out(priority_encoder_1_out));  // open: gs, en_out, en_in
  Pull_Resistor #(.pull(0)) pull_resistor_2 (.node(priority_encoder_1_out));
  Multiplexer #(.select(2), .width(32), .disabled("Z"), .enable("false")) multiplexer_1 (
    .in0(adder_1_out), .in1(adder_2_out), .in2(subtractor_1_out), .in3({{31{1'b0}}, comparator_1_lt[0]}),
    .out(Result), .sel(priority_encoder_1_out));

  // Notes on the sheet:
  //   不要改变此引脚区域内容，也不要改变ALU封装形式
  //   输入引脚
  //   输出引脚
endmodule

// 中断控制器
module \中断控制器  (
  input  CLK,
  input  Key1,
  input  Key2,
  input  Key3,
  input  Clr,
  input  [1:0] EDU_TEST,
  output IR1W,
  output IR2W,
  output IR3W,
  output [1:0] IntNo,
  output IntR
);

  wire and_1_out, and_2_out, and_3_out, Clr0, Clr1, Clr2, Clr3, d_ff_1_q, d_ff_2_q, d_ff_3_q, IR1_q, IR2_q,
       IR3_q, or_1_out, or_3_out, or_6_out, or_7_out, or_8_out;

  or or_1 (or_1_out, Key1, EDU_TEST[0]);
  or or_2 (IR1W, IR1_q, d_ff_2_q);
  or or_3 (or_3_out, Key2, EDU_TEST[1]);
  or or_4 (IR2W, IR2_q, d_ff_3_q);
  D_Flip_Flop #(.trigger("rising"), .Pre_Clr_Positions("LEGACY"), .NegatePresetClear("false"), .enable("true"), .NewFFLayout("false")) d_ff_1 (
    .clk(Key3), .D(1'b1), .Q(d_ff_1_q), .reset(IR3_q));  // open: Qn, preset, en
  or or_5 (IR3W, IR3_q, d_ff_1_q);
  D_Flip_Flop #(.trigger("rising"), .Pre_Clr_Positions("LEGACY"), .NegatePresetClear("false"), .enable("true"), .NewFFLayout("false")) d_ff_2 (
    .clk(or_1_out), .D(1'b1), .Q(d_ff_2_q), .reset(IR1_q));  // open: Qn, preset, en
  D_Flip_Flop #(.trigger("rising"), .Pre_Clr_Positions("LEGACY"), .NegatePresetClear("false"), .enable("true"), .NewFFLayout("false")) d_ff_3 (
    .clk(or_3_out), .D(1'b1), .Q(d_ff_3_q), .reset(IR2_q));  // open: Qn, preset, en
  or or_6 (or_6_out, d_ff_2_q, IR1_q);
  and and_1 (and_1_out, or_6_out, ~Clr1);  // AND_Gate
  or or_7 (or_7_out, d_ff_3_q, IR2_q);
  and and_2 (and_2_out, or_7_out, ~Clr2);  // AND_Gate
  or or_8 (or_8_out, d_ff_1_q, IR3_q);
  and and_3 (and_3_out, or_8_out, ~Clr3);  // AND_Gate
  Pull_Resistor #(.pull(0)) pull_resistor_1 (.node(EDU_TEST));
  D_Flip_Flop #(.trigger("rising"), .Pre_Clr_Positions("LEGACY"), .NegatePresetClear("false"), .enable("true"), .NewFFLayout("false")) IR1 (
    .clk(CLK), .D(and_1_out), .Q(IR1_q));  // open: Qn, preset, en, reset
  D_Flip_Flop #(.trigger("rising"), .Pre_Clr_Positions("LEGACY"), .NegatePresetClear("false"), .enable("true"), .NewFFLayout("false")) IR2 (
    .clk(CLK), .D(and_2_out), .Q(IR2_q));  // open: Qn, preset, en, reset
  D_Flip_Flop #(.trigger("rising"), .Pre_Clr_Positions("LEGACY"), .NegatePresetClear("false"), .enable("true"), .NewFFLayout("false")) IR3 (
    .clk(CLK), .D(and_3_out), .Q(IR3_q));  // open: Qn, preset, en, reset
  Priority_Encoder #(.select(2), .disabled("Z")) priority_encoder_1 (
    .in1(IR1_q), .in2(IR2_q), .in3(IR3_q), .out(IntNo), .gs(IntR));  // open: in0, en_out, en_in
  Decoder #(.select(2), .tristate("false"), .disabled(0), .enable("true")) decoder_1 (
    .out0(Clr0), .out1(Clr1), .out2(Clr2), .out3(Clr3), .sel(IntNo), .en(Clr));

  // Other names for the same wires on the sheet: EDU_INT1 = EDU_TEST[0]; EDU_INT2 = EDU_TEST[1]

  // Notes on the sheet:
  //   中断等待
  //   中断等待
  //   中断等待
  //   中断信号采样参考电路
  //   Reset 
  //   Reset 
  //   Reset 
  //   中断优先编码器
endmodule
